# Fritzing sketch Electronic skech (saved by Fritzing 0.9.5d)
breadboards: 2

parts:
  U1 = LuaNode32 / ESP32 [part_number=ESP32S-PIN30]
  hc-sr1 = hc-sr04
  U2 = LuaNode32 / ESP32 [part_number=ESP32S-PIN30]
  RHT1 = Humidity and Temperature Sensor RHT03
  R2 = Resistor [tolerance=±5% resistance=10k package="2512 [SMD]"]
  Q1 = MOSFET-NCHANNEL [package=to-92]
  R3 = Resistor [tolerance=±5% resistance=1000 package="2512 [SMD]"]
  J1 = Peltier Element
  HLK-PM1 = HLK-PM12 [part_number=HLK-PM12]
  R4 = Resistor [tolerance=±5% resistance=1000 package="2512 [SMD]"]
  RHT2 = Humidity and Temperature Sensor RHT03
  R5 = Resistor [tolerance=±5% resistance=10k package="2512 [SMD]"]
  LCD1 = 2.8" SPI TFT Module [part_number=MSP2807]  # not connected

nets:
  VCC: U1.3V3, hc-sr1.VCC, RHT1.Vcc, R2.Pin_0
  GND: U1.GND, hc-sr1.GND, RHT1.GND_2
  N1: U1.D4, RHT1.Data-signal, R2.Pin_1
  N2: U1.D5, hc-sr1.Trig
  N3: U1.D18, hc-sr1.Echo
  N4: U2.D26, R5.Pin_1
  N5: U2.D27, R3.Pin_1
  N6: U2.GND, R4.Pin_1
  3V3: U2.3V3, RHT2.Vcc
  N7: Q1.D, J1.pin1
  N8: Q1.S, HLK-PM1.-Vo, R4.Pin_0, RHT2.GND_2
  N9: Q1.G, R3.Pin_0
  N10: J1.pin2, HLK-PM1.+Vo
  N11: RHT2.Data-signal, R5.Pin_0

custom parts:
  LuaNode32 / ESP32: New Image for LuaNode32 DOIT ESP32 DEVKIT V1. Base parts from LuaNode32 / ESP32 ESP32 based LuaNode32 by G.Noorlander DOIT Esp32 DevKit v1 (30 pins long, 11 pins width) by Werner Rothschopf (modified by vanepp Dec 2018)
  2.8" SPI TFT Module: A generic 2.8 inch LCD TFT 320x240 display with touchscreen and SD card slot. Uses the ILI9341 controller, like the Adafruit displays of this size uses.
